# Fritzing sketch Vedlegg 2 - Fritzing (saved by Fritzing 0.9.3b)
breadboards: 1

parts:
  Part1 = Photon
  KEYPAD1 = Membrane Matrix Keypad
  J1 = Basic Servo
  Part2 = LCD1602-I2C

nets:
  N1: Part1.A1, KEYPAD1.5
  N2: Part1.A2, KEYPAD1.6
  N3: Part1.A3, KEYPAD1.7
  N4: Part1.A4, J1.pulse
  GND: Part1.GND, J1.gnd, Part2.GND
  VCC: Part1.VIN, J1.vcc, Part2.VCC
  N5: Part1.D0, Part2.SDA
  N6: Part1.D1, Part2.SCL
  N7: Part1.D2, KEYPAD1.1
  N8: Part1.D3, KEYPAD1.2
  N9: Part1.D4, KEYPAD1.3
  N10: Part1.D5, KEYPAD1.4

custom parts:
  Membrane Matrix Keypad: Membrane Matrix 3x4 Keypad
  LCD1602-I2C: A standard character display, usually with 2x16 characters. Comes in many colors with LCM1602 IIC attached.
